# Fritzing sketch sumo (saved by Fritzing 0.9.3b)

parts:
  Linh_kiện1 = Arduino Uno (Rev3) - ICSP
  L298N1 = L298N DC motor driver
  M1 = DC Motor
  M2 = DC Motor
  hc-sr1 = hc-sr04
  hc-sr2 = hc-sr04
  VCC1 = 4 x AAA Battery Mount
  M3 = fc-51 [package=THT]
  M4 = fc-51 [package=THT]
  M5 = fc-51 [package=THT]

nets:
  N1: Linh_kiện1.A0, M3.pin1
  N2: Linh_kiện1.A1, M4.pin1
  N3: Linh_kiện1.A2, M5.pin1
  N4: Linh_kiện1.ICSP_MOSI, Linh_kiện1.D11_PWM/MOSI, L298N1.IN1
  GND: Linh_kiện1.GND, L298N1.GND, hc-sr1.GND, VCC1.-
  N5: Linh_kiện1.D8, L298N1.IN3
  N6: Linh_kiện1.D9_PWM, L298N1.ENB
  N7: Linh_kiện1.D10_PWM/SS, L298N1.IN2
  N8: Linh_kiện1.D12/MISO, L298N1.ENA
  N9: Linh_kiện1.D3_PWM, hc-sr2.Echo
  N10: Linh_kiện1.D4, hc-sr2.Trig
  N11: Linh_kiện1.D5_PWM, hc-sr1.Echo
  N12: Linh_kiện1.D6_PWM, hc-sr1.Trig
  N13: Linh_kiện1.D7, L298N1.IN4
  VIN: Linh_kiện1.VIN, L298N1.5V
  N14: L298N1.OUT1, M1.pin_2
  N15: L298N1.OUT2, M1.pin_1
  N16: L298N1.OUT3, M2.pin_2
  N17: L298N1.OUT4, M2.pin_1
  N18: L298N1.12V, VCC1.+
  VCC: hc-sr1.VCC, hc-sr2.VCC
  N19: M4.pin2, M5.pin2
  N20: M4.pin3, M5.pin3

custom parts:
  L298N DC motor driver: 2x DC motor driver with 78M05 positive voltage regulator (7..35 V) L298N: max 46 V, 2 A Set 5 V Enable jumper to enable 5 V regultor (needed for the L298N) and +5 V output at screw terminal or supply external +5 V at screw terminal Set ENA and/or ENB to +5 V to enable motor permanently or supply ENA and/or ENB with PWM signal IN1 and IN2 set rotation directory for motor A (OUT1/OUT2) IN2 and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
